// Logisim project Risc V.circ as structural Verilog: 11 circuits, main circuit main
module main (
);

  wire alu_1_branchfromalu, clock_1_out, comparator_1_eq, ex_mem_1_branchfromalu_2, EX_MEM_RegWrite, Flush,
       ID_EX_MemRead, IF_ID_branch, MEM_WB_RegWrite, not_1_out, nStall;
  wire [0:0] ex_mem_1_wb_2, id_ex_1_ex, mem_wb_1_wb_2;
  wire [1:0] cu_1_immsel, Forward_A, Forward_B, id_ex_1_wb;
  wire [2:0] cu_1_aluop, ex_mem_1_m_2, id_ex_1_ex_2;
  wire [2:1] id_ex_1_m;
  wire [3:0] ex_mem_1_data_b_2, ex_mem_1_data_b_2_3, id_ex_1__30_14_12_instructions_2;
  wire [4:0] cu_1_alusrc, ex_mem_1__11_7_instructions_2, id_ex_1_rs1_2, id_ex_1_rs2_2, ID_EX_Rd, IF_ID_Rs1,
       IF_ID_Rs2, mem_wb_1__11_7_instructions_2;
  wire [6:0] bit_extender_1_out;
  wire [8:0] multiplexer_2_out;
  wire [31:0] adder_1_out, adder_2_out, alu_1_alu_result, ex_mem_1_addsum_2, ex_mem_1_alu_result_2,
       id_ex_1_data_a_2, id_ex_1_data_b_2, id_ex_1_imm_gen_2, id_ex_1_pc_2, if_id_1_instructions_2,
       if_id_1_pc_2, imm_gen_1_out, mem_wb_1_alu_result_2, mem_wb_1_read_data_2, multiplexer_1_out,
       multiplexer_3_out, multiplexer_4_out, multiplexer_5_out, multiplexer_6_out, PC_q, ram_1_data,
       ram_2_data, resgiterfile_1_data_a, resgiterfile_1_data_b, shifter_1_out;
  wire [31:4] ex_mem_1_data_b_2_2;

  Multiplexer #(.width(32), .disabled(0), .enable("false")) multiplexer_1 (
    .in0(adder_1_out), .in1(ex_mem_1_addsum_2), .out(multiplexer_1_out), .sel(Flush));
  Register #(.width(32)) PC (.D(multiplexer_1_out), .en(nStall), .Q(PC_q), .clk(not_1_out));  // open: clr
  not not_1 (not_1_out, clock_1_out);
  Adder #(.width(32)) adder_1 (.a(32'h1), .b(PC_q), .out(adder_1_out));  // open: cin, cout
  Clock clock_1 (.out(clock_1_out));
  RAM #(.addrWidth(24), .dataWidth(32)) ram_1 (
    .addr(PC_q[23:0]), .data(ram_1_data), .clk(clock_1_out));  // open: sel, ld, clr
  hazard_Detection_Unit hazard_detection_unit_1 (
    .Mem_Read(ID_EX_MemRead), .Rs1(IF_ID_Rs1), .Rs2(IF_ID_Rs2), .Rd(ID_EX_Rd), .nStall(nStall));
  IF_ID if_id_1 (
    .PC(PC_q), .PC_2(if_id_1_pc_2), .Instructions(ram_1_data),
    .Instructions_2({if_id_1_instructions_2[31:25], IF_ID_Rs2, IF_ID_Rs1, if_id_1_instructions_2[14:0]}),
    .clock(clock_1_out), .Enable(nStall));
  CU cu_1 (
    .Opcode(if_id_1_instructions_2[6:0]), .ImmSel(cu_1_immsel), .ALUSrc(cu_1_alusrc[0]),
    .MemtoReg(cu_1_alusrc[1]), .RegWrite(cu_1_alusrc[2]), .MemRead(cu_1_alusrc[3]),
    .MemWrite(cu_1_alusrc[4]), .Branch(IF_ID_branch), .AluOP(cu_1_aluop));
  Imm_Gen imm_gen_1 (
    .Instruction({if_id_1_instructions_2[31:25], IF_ID_Rs2, IF_ID_Rs1, if_id_1_instructions_2[14:0]}),
    .OUT(imm_gen_1_out), .ImmSel(cu_1_immsel));
  Multiplexer #(.width(9), .disabled(0), .enable("false")) multiplexer_2 (
    .in0({9{1'b0}}), .in1({cu_1_aluop, IF_ID_branch, cu_1_alusrc}), .out(multiplexer_2_out), .sel(nStall));
  resgiterFile resgiterfile_1 (
    .Data_D(multiplexer_6_out), .Reg_Write_Enable(MEM_WB_RegWrite), .Addr_D(mem_wb_1__11_7_instructions_2),
    .Data_A(resgiterfile_1_data_a), .Data_B(resgiterfile_1_data_b), .Addr_B(IF_ID_Rs2), .Addr_A(IF_ID_Rs1),
    .Clock(clock_1_out));
  Hex_Digit_Display hex_digit_display_1 (.value(ex_mem_1_data_b_2_2[31:28]));  // open: dp
  Hex_Digit_Display hex_digit_display_2 (.value(ex_mem_1_data_b_2_2[27:24]));  // open: dp
  ID_EX id_ex_1 (
    .ALUSrc(multiplexer_2_out[0]), .MemtoReg(multiplexer_2_out[1]), .RegWrite(multiplexer_2_out[2]),
    .MemRead(multiplexer_2_out[3]), .MemWrite(multiplexer_2_out[4]), .Branch(multiplexer_2_out[5]),
    .AluOP(multiplexer_2_out[8:6]), .Clock(clock_1_out), .Data_A(resgiterfile_1_data_a),
    .Data_B(resgiterfile_1_data_b), .Imm_Gen(imm_gen_1_out),
    ._30_14_12_Instructions({if_id_1_instructions_2[30], if_id_1_instructions_2[14:12]}),
    ._11_7_Instructions(if_id_1_instructions_2[11:7]), .WB(id_ex_1_wb), .M({id_ex_1_m, ID_EX_MemRead}),
    .EX({id_ex_1_ex_2, id_ex_1_ex[0]}), .Data_A_2(id_ex_1_data_a_2), .Data_B_2(id_ex_1_data_b_2),
    .Imm_Gen_2(id_ex_1_imm_gen_2), ._30_14_12_Instructions_2(id_ex_1__30_14_12_instructions_2),
    ._11_7_Instructions_2(ID_EX_Rd), .PC(if_id_1_pc_2), .PC_2(id_ex_1_pc_2), .Rs1(IF_ID_Rs1),
    .Rs1_2(id_ex_1_rs1_2), .Rs2(IF_ID_Rs2), .Rs2_2(id_ex_1_rs2_2), .clear(Flush));
  Hex_Digit_Display hex_digit_display_3 (.value(ex_mem_1_data_b_2_2[23:20]));  // open: dp
  Hex_Digit_Display hex_digit_display_4 (.value(ex_mem_1_data_b_2_2[19:16]));  // open: dp
  Multiplexer #(.select(2), .width(32), .disabled(0), .enable("false")) multiplexer_3 (
    .in0(id_ex_1_data_a_2), .in1(multiplexer_6_out), .in2(ex_mem_1_alu_result_2), .out(multiplexer_3_out),
    .sel(Forward_A));  // open: in3
  Multiplexer #(.select(2), .width(32), .disabled(0), .enable("false")) multiplexer_4 (
    .in0(id_ex_1_data_b_2), .in1(multiplexer_6_out), .in2(ex_mem_1_alu_result_2), .out(multiplexer_4_out),
    .sel(Forward_B));  // open: in3
  Hex_Digit_Display hex_digit_display_5 (.value(ex_mem_1_data_b_2_2[15:12]));  // open: dp
  Hex_Digit_Display hex_digit_display_6 (.value(ex_mem_1_data_b_2_3));  // open: dp
  Shifter #(.width(32), .shift("ar")) shifter_1 (.in(id_ex_1_imm_gen_2), .\dist (5'b00010), .out(shifter_1_out));
  Multiplexer #(.width(32), .disabled(0), .enable("false")) multiplexer_5 (
    .in0(multiplexer_4_out), .in1(id_ex_1_imm_gen_2), .out(multiplexer_5_out), .sel(id_ex_1_ex[0]));
  forward_Unit forward_unit_1 (
    .EX_MEM_RegWrite(EX_MEM_RegWrite), .EX_MEM_Rd(ex_mem_1__11_7_instructions_2), .ID_EX_Rs1(id_ex_1_rs1_2),
    .ID_EX_Rs2(id_ex_1_rs2_2), .MEM_WB_RegWrite(MEM_WB_RegWrite), .MEM_WB_Rd(mem_wb_1__11_7_instructions_2),
    .Forward_A(Forward_A), .Forward_B(Forward_B));
  Hex_Digit_Display hex_digit_display_7 (.value(ex_mem_1_data_b_2_2[7:4]));  // open: dp
  Adder #(.width(32)) adder_2 (.a(id_ex_1_pc_2), .b(shifter_1_out), .out(adder_2_out));  // open: cin, cout
  Hex_Digit_Display hex_digit_display_8 (.value(ex_mem_1_data_b_2));  // open: dp
  ALU alu_1 (
    .branchFromALU(alu_1_branchfromalu), .ALU_Result(alu_1_alu_result), .Data_A(multiplexer_3_out),
    .func7_func3(id_ex_1__30_14_12_instructions_2), .Data_B(multiplexer_5_out), .ALUOP(id_ex_1_ex_2));
  EX_MEM ex_mem_1 (
    .WB(id_ex_1_wb), .M({id_ex_1_m, ID_EX_MemRead}), .AddSum(adder_2_out),
    .branchFromALU(alu_1_branchfromalu), .ALU_Result(alu_1_alu_result), .Data_B(multiplexer_4_out),
    ._11_7_Instructions(ID_EX_Rd), .WB_2({EX_MEM_RegWrite, ex_mem_1_wb_2[0]}), .M_2(ex_mem_1_m_2),
    .AddSum_2(ex_mem_1_addsum_2), .branchFromALU_2(ex_mem_1_branchfromalu_2),
    .ALU_Result_2(ex_mem_1_alu_result_2),
    .Data_B_2({ex_mem_1_data_b_2_2[31:12], ex_mem_1_data_b_2_3, ex_mem_1_data_b_2_2[7:4], ex_mem_1_data_b_2}),
    ._11_7_Instructions_2(ex_mem_1__11_7_instructions_2), .Clock(clock_1_out));
  and and_1 (Flush, ex_mem_1_m_2[2], ex_mem_1_branchfromalu_2);
  Bit_Extender #(.in_width(32), .out_width(7), .\type ("sign")) bit_extender_1 (
    .in({ex_mem_1_data_b_2_2[31:12], ex_mem_1_data_b_2_3, ex_mem_1_data_b_2_2[7:4], ex_mem_1_data_b_2}),
    .out(bit_extender_1_out));
  Comparator #(.width(24)) comparator_1 (
    .a(ex_mem_1_alu_result_2[23:0]), .b({24{1'b1}}), .eq(comparator_1_eq));  // open: gt, lt
  RAM #(.addrWidth(24), .dataWidth(32), .bus("separate")) ram_2 (
    .addr(ex_mem_1_alu_result_2[23:0]),
    .din({ex_mem_1_data_b_2_2[31:12], ex_mem_1_data_b_2_3, ex_mem_1_data_b_2_2[7:4], ex_mem_1_data_b_2}),
    .data(ram_2_data), .str(ex_mem_1_m_2[1]), .clk(clock_1_out), .ld(ex_mem_1_m_2[0]));  // open: sel, clr
  TTY tty_1 (.data(bit_extender_1_out), .clk(clock_1_out), .we(comparator_1_eq));  // open: clr
  MEM_WB mem_wb_1 (
    .WB({EX_MEM_RegWrite, ex_mem_1_wb_2[0]}), .Read_Data(ram_2_data), .ALU_Result(ex_mem_1_alu_result_2),
    ._11_7_Instructions(ex_mem_1__11_7_instructions_2), .WB_2({MEM_WB_RegWrite, mem_wb_1_wb_2[0]}),
    .Read_Data_2(mem_wb_1_read_data_2), .ALU_Result_2(mem_wb_1_alu_result_2),
    ._11_7_Instructions_2(mem_wb_1__11_7_instructions_2), .Clock(clock_1_out));
  Multiplexer #(.width(32), .disabled(0), .enable("false")) multiplexer_6 (
    .in0(mem_wb_1_alu_result_2), .in1(mem_wb_1_read_data_2), .out(multiplexer_6_out), .sel(mem_wb_1_wb_2[0]));

  // Notes on the sheet:
  //   Instruction MEM
endmodule

module resgiterFile (
  input  [31:0] Data_D,
  input  [4:0] Addr_A,
  input  Clock,
  input  [4:0] Addr_B,
  input  Reg_Write_Enable,
  input  [4:0] Addr_D,
  output [31:0] Data_A,
  output [31:0] Data_B
);

  wire demultiplexer_1_out0, demultiplexer_1_out1, demultiplexer_1_out2, demultiplexer_1_out3,
       demultiplexer_1_out4, demultiplexer_1_out5, demultiplexer_1_out6, demultiplexer_1_out7,
       demultiplexer_1_out8, demultiplexer_1_out9, demultiplexer_1_out10, demultiplexer_1_out11,
       demultiplexer_1_out12, demultiplexer_1_out13, demultiplexer_1_out14, demultiplexer_1_out15,
       demultiplexer_1_out16, demultiplexer_1_out17, demultiplexer_1_out18, demultiplexer_1_out19,
       demultiplexer_1_out20, demultiplexer_1_out21, demultiplexer_1_out22, demultiplexer_1_out23,
       demultiplexer_1_out24, demultiplexer_1_out25, demultiplexer_1_out26, demultiplexer_1_out27,
       demultiplexer_1_out28, demultiplexer_1_out29, demultiplexer_1_out30, demultiplexer_1_out31, not_1_out;
  wire [31:0] r0_q, r1_q, r2_q, r3_q, r4_q, r5_q, r6_q, r7_q, r8_q, r9_q, r10_q, r11_q, r12_q, r13_q, r14_q,
       r15_q, r16_q, r17_q, r18_q, r19_q, r20_q, r21_q, r22_q, r23_q, r24_q, r25_q, r26_q, r27_q, r28_q,
       r29_q, r31_q, r32_q;

  not not_1 (not_1_out, Clock);
  Demultiplexer #(.select(5), .disabled(0)) demultiplexer_1 (
    .out0(demultiplexer_1_out0), .out1(demultiplexer_1_out1), .out2(demultiplexer_1_out2),
    .out3(demultiplexer_1_out3), .out4(demultiplexer_1_out4), .out5(demultiplexer_1_out5),
    .out6(demultiplexer_1_out6), .out7(demultiplexer_1_out7), .out8(demultiplexer_1_out8),
    .out9(demultiplexer_1_out9), .out10(demultiplexer_1_out10), .out11(demultiplexer_1_out11),
    .out12(demultiplexer_1_out12), .out13(demultiplexer_1_out13), .out14(demultiplexer_1_out14),
    .out15(demultiplexer_1_out15), .out16(demultiplexer_1_out16), .out17(demultiplexer_1_out17),
    .out18(demultiplexer_1_out18), .out19(demultiplexer_1_out19), .out20(demultiplexer_1_out20),
    .out21(demultiplexer_1_out21), .out22(demultiplexer_1_out22), .out23(demultiplexer_1_out23),
    .out24(demultiplexer_1_out24), .out25(demultiplexer_1_out25), .out26(demultiplexer_1_out26),
    .out27(demultiplexer_1_out27), .out28(demultiplexer_1_out28), .out29(demultiplexer_1_out29),
    .out30(demultiplexer_1_out30), .out31(demultiplexer_1_out31), .in(Reg_Write_Enable), .sel(Addr_D),
    .en(Reg_Write_Enable));
  Register #(.width(32)) r0 (.D(Data_D), .en(demultiplexer_1_out0), .Q(r0_q), .clk(not_1_out));  // open: clr
  Register #(.width(32)) r4 (.D(Data_D), .en(demultiplexer_1_out4), .Q(r4_q), .clk(not_1_out));  // open: clr
  Register #(.width(32)) r8 (.D(Data_D), .en(demultiplexer_1_out8), .Q(r8_q), .clk(not_1_out));  // open: clr
  Register #(.width(32)) r12 (.D(Data_D), .en(demultiplexer_1_out12), .Q(r12_q), .clk(not_1_out));  // open: clr
  Register #(.width(32)) r16 (.D(Data_D), .en(demultiplexer_1_out16), .Q(r16_q), .clk(not_1_out));  // open: clr
  Register #(.width(32)) r20 (.D(Data_D), .en(demultiplexer_1_out20), .Q(r20_q), .clk(not_1_out));  // open: clr
  Register #(.width(32)) r1 (.D(Data_D), .en(demultiplexer_1_out1), .Q(r1_q), .clk(not_1_out));  // open: clr
  Register #(.width(32)) r5 (.D(Data_D), .en(demultiplexer_1_out5), .Q(r5_q), .clk(not_1_out));  // open: clr
  Register #(.width(32)) r24 (.D(Data_D), .en(demultiplexer_1_out24), .Q(r24_q), .clk(not_1_out));  // open: clr
  Register #(.width(32)) r28 (.D(Data_D), .en(demultiplexer_1_out28), .Q(r28_q), .clk(not_1_out));  // open: clr
  Register #(.width(32)) r9 (.D(Data_D), .en(demultiplexer_1_out9), .Q(r9_q), .clk(not_1_out));  // open: clr
  Register #(.width(32)) r13 (.D(Data_D), .en(demultiplexer_1_out13), .Q(r13_q), .clk(not_1_out));  // open: clr
  Register #(.width(32)) r17 (.D(Data_D), .en(demultiplexer_1_out17), .Q(r17_q), .clk(not_1_out));  // open: clr
  Register #(.width(32)) r21 (.D(Data_D), .en(demultiplexer_1_out21), .Q(r21_q), .clk(not_1_out));  // open: clr
  Register #(.width(32)) r25 (.D(Data_D), .en(demultiplexer_1_out25), .Q(r25_q), .clk(not_1_out));  // open: clr
  Register #(.width(32)) r29 (.D(Data_D), .en(demultiplexer_1_out29), .Q(r29_q), .clk(not_1_out));  // open: clr
  Register #(.width(32)) r2 (.D(Data_D), .en(demultiplexer_1_out2), .Q(r2_q), .clk(not_1_out));  // open: clr
  Register #(.width(32)) r6 (.D(Data_D), .en(demultiplexer_1_out6), .Q(r6_q), .clk(not_1_out));  // open: clr
  Register #(.width(32)) r10 (.D(Data_D), .en(demultiplexer_1_out10), .Q(r10_q), .clk(not_1_out));  // open: clr
  Register #(.width(32)) r14 (.D(Data_D), .en(demultiplexer_1_out14), .Q(r14_q), .clk(not_1_out));  // open: clr
  Register #(.width(32)) r18 (.D(Data_D), .en(demultiplexer_1_out18), .Q(r18_q), .clk(not_1_out));  // open: clr
  Register #(.width(32)) r22 (.D(Data_D), .en(demultiplexer_1_out22), .Q(r22_q), .clk(not_1_out));  // open: clr
  Register #(.width(32)) r26 (.D(Data_D), .en(demultiplexer_1_out26), .Q(r26_q), .clk(not_1_out));  // open: clr
  Register #(.width(32)) r3 (.D(Data_D), .en(demultiplexer_1_out3), .Q(r3_q), .clk(not_1_out));  // open: clr
  Register #(.width(32)) r7 (.D(Data_D), .en(demultiplexer_1_out7), .Q(r7_q), .clk(not_1_out));  // open: clr
  Register #(.width(32)) r11 (.D(Data_D), .en(demultiplexer_1_out11), .Q(r11_q), .clk(not_1_out));  // open: clr
  Register #(.width(32)) r31 (.D(Data_D), .en(demultiplexer_1_out30), .Q(r31_q), .clk(not_1_out));  // open: clr
  Register #(.width(32)) r15 (.D(Data_D), .en(demultiplexer_1_out15), .Q(r15_q), .clk(not_1_out));  // open: clr
  Register #(.width(32)) r19 (.D(Data_D), .en(demultiplexer_1_out19), .Q(r19_q), .clk(not_1_out));  // open: clr
  Register #(.width(32)) r23 (.D(Data_D), .en(demultiplexer_1_out23), .Q(r23_q), .clk(not_1_out));  // open: clr
  Register #(.width(32)) r27 (.D(Data_D), .en(demultiplexer_1_out27), .Q(r27_q), .clk(not_1_out));  // open: clr
  Register #(.width(32)) r32 (.D(Data_D), .en(demultiplexer_1_out31), .Q(r32_q), .clk(not_1_out));  // open: clr
  Multiplexer #(.select(5), .width(32), .disabled(0), .enable("false")) multiplexer_1 (
    .in0(r0_q), .in1(r1_q), .in2(r2_q), .in3(r3_q), .in4(r4_q), .in5(r5_q), .in6(r6_q), .in7(r7_q),
    .in8(r8_q), .in9(r9_q), .in10(r10_q), .in11(r11_q), .in12(r12_q), .in13(r13_q), .in14(r14_q),
    .in15(r15_q), .in16(r16_q), .in17(r17_q), .in18(r18_q), .in19(r19_q), .in20(r20_q), .in21(r21_q),
    .in22(r22_q), .in23(r23_q), .in24(r24_q), .in25(r25_q), .in26(r26_q), .in27(r27_q), .in28(r28_q),
    .in29(r29_q), .in30(r31_q), .in31(r32_q), .out(Data_A), .sel(Addr_A));
  Multiplexer #(.select(5), .width(32), .disabled(0), .enable("false")) multiplexer_2 (
    .in0(r0_q), .in1(r1_q), .in2(r2_q), .in3(r3_q), .in4(r4_q), .in5(r5_q), .in6(r6_q), .in7(r7_q),
    .in8(r8_q), .in9(r9_q), .in10(r10_q), .in11(r11_q), .in12(r12_q), .in13(r13_q), .in14(r14_q),
    .in15(r15_q), .in16(r16_q), .in17(r17_q), .in18(r18_q), .in19(r19_q), .in20(r20_q), .in21(r21_q),
    .in22(r22_q), .in23(r23_q), .in24(r24_q), .in25(r25_q), .in26(r26_q), .in27(r27_q), .in28(r28_q),
    .in29(r29_q), .in30(r31_q), .in31(r32_q), .out(Data_B), .sel(Addr_B));
endmodule

module ALU (
  input  [31:0] Data_A,
  input  [2:0] ALUOP,
  input  [31:0] Data_B,
  input  [3:0] func7_func3,
  output branchFromALU,
  output [31:0] ALU_Result
);

  wire comparator_1_eq, comparator_1_gt, comparator_1_lt, not_1_out, or_2_out;
  wire [31:0] adder_1_out, and_1_out, multiplexer_1_out, multiplexer_2_out, or_1_out, subtractor_1_out,
       undriven, xor_1_out;

  assign xor_1_out = Data_A ^ Data_B;  // XOR_Gate xor_1, 32 bits wide
  assign or_1_out = Data_A | Data_B;  // OR_Gate or_1, 32 bits wide
  assign and_1_out = Data_A & Data_B;  // AND_Gate and_1, 32 bits wide
  Adder #(.width(32)) adder_1 (.a(Data_A), .b(Data_B), .out(adder_1_out));  // open: cin, cout
  Subtractor #(.width(32)) subtractor_1 (.a(Data_A), .b(Data_B), .out(subtractor_1_out));  // open: bin, bout
  Multiplexer #(.width(32), .disabled(0), .enable("false")) multiplexer_1 (
    .in0(adder_1_out), .in1(subtractor_1_out), .out(multiplexer_1_out), .sel(func7_func3[3]));
  Multiplexer #(.select(3), .width(32), .enable("false")) multiplexer_2 (
    .in0(multiplexer_1_out), .in1(undriven), .in2(undriven), .in3(undriven), .in4(xor_1_out), .in5(undriven),
    .in6(or_1_out), .in7(and_1_out), .out(multiplexer_2_out), .sel(func7_func3[2:0]));
  Comparator #(.width(32)) comparator_1 (
    .a(Data_A), .b(Data_B), .gt(comparator_1_gt), .eq(comparator_1_eq), .lt(comparator_1_lt));
  Multiplexer #(.select(2), .width(32), .disabled(0), .enable("false")) multiplexer_3 (
    .in0(adder_1_out), .in1(subtractor_1_out), .in2(multiplexer_2_out), .in3(undriven), .out(ALU_Result),
    .sel(ALUOP[1:0]));
  not not_1 (not_1_out, comparator_1_eq);
  or or_2 (or_2_out, comparator_1_eq, comparator_1_gt);
  Multiplexer #(.select(3), .disabled(0), .enable("false")) multiplexer_4 (
    .in0(comparator_1_eq), .in1(not_1_out), .in2(1'b0), .in3(1'b0), .in4(comparator_1_lt), .in5(or_2_out),
    .in6(1'b0), .in7(1'b0), .out(branchFromALU), .sel(func7_func3[2:0]));
endmodule

// Control Unit
module CU (
  input  [6:0] Opcode,
  output [1:0] ImmSel,
  output ALUSrc,
  output MemtoReg,
  output RegWrite,
  output MemRead,
  output MemWrite,
  output Branch,
  output [2:0] AluOP
);

  wire [4:0] comparator_1_eq;

  Comparator #(.width(7)) comparator_1 (.a(Opcode), .b(7'b0110011), .eq(comparator_1_eq[0]));  // open: gt, lt
  Comparator #(.width(7)) comparator_2 (.a(Opcode), .b(7'b0010011), .eq(comparator_1_eq[1]));  // open: gt, lt
  Comparator #(.width(7)) comparator_3 (.a(Opcode), .b(7'b0000011), .eq(comparator_1_eq[2]));  // open: gt, lt
  Comparator #(.width(7)) comparator_4 (.a(Opcode), .b(7'b0100011), .eq(comparator_1_eq[3]));  // open: gt, lt
  Comparator #(.width(7)) comparator_5 (.a(Opcode), .b(7'b1100011), .eq(comparator_1_eq[4]));  // open: gt, lt
  Multiplexer #(.select(5), .width(11), .disabled(0), .enable("false")) multiplexer_1 (
    .in0({11{1'b0}}), .in1(11'h210), .in2(11'h214), .in3({11{1'b0}}), .in4(11'h3d), .in5({11{1'b0}}),
    .in6({11{1'b0}}), .in7({11{1'b0}}), .in8(11'h45), .in9({11{1'b0}}), .in10({11{1'b0}}), .in11({11{1'b0}}),
    .in12({11{1'b0}}), .in13({11{1'b0}}), .in14({11{1'b0}}), .in15({11{1'b0}}), .in16(11'h482),
    .in17({11{1'b0}}), .in18({11{1'b0}}), .in19({11{1'b0}}), .in20({11{1'b0}}), .in21({11{1'b0}}),
    .in22({11{1'b0}}), .in23({11{1'b0}}), .in24({11{1'b0}}), .in25({11{1'b0}}), .in26({11{1'b0}}),
    .in27({11{1'b0}}), .in28({11{1'b0}}), .in29({11{1'b0}}), .in30({11{1'b0}}), .in31({11{1'b0}}),
    .out({AluOP[0], AluOP[1], AluOP[2], Branch, MemWrite, MemRead, RegWrite, MemtoReg, ALUSrc, ImmSel}),
    .sel(comparator_1_eq));
endmodule

module Imm_Gen (
  input  [31:0] Instruction,
  input  [1:0] ImmSel,
  output [31:0] OUT
);

  Multiplexer #(.select(2), .width(32), .disabled(0), .enable("false")) multiplexer_1 (
    .in0({{21{Instruction[31]}}, Instruction[30:20]}),
    .in1({{21{Instruction[31]}}, Instruction[30:25], Instruction[11:7]}),
    .in2({{20{Instruction[31]}}, Instruction[7], Instruction[30:25], Instruction[11:8], 1'b0}),
    .in3({32{1'b0}}), .out(OUT), .sel(ImmSel));

  // Notes on the sheet:
  //   I-Type
  //   S-Type
  //   B-Type
endmodule

module IF_ID (
  input  [31:0] PC,
  input  [31:0] Instructions,
  input  clock,
  input  Enable,
  output [31:0] PC_2,
  output [31:0] Instructions_2
);

  Register #(.width(32)) register_1 (.D(PC), .en(Enable), .Q(PC_2), .clk(clock));  // open: clr
  Register #(.width(32)) register_2 (.D(Instructions), .en(Enable), .Q(Instructions_2), .clk(clock));  // open: clr
endmodule

module ID_EX (
  input  ALUSrc,
  input  MemtoReg,
  input  RegWrite,
  input  MemRead,
  input  MemWrite,
  input  Branch,
  input  [31:0] PC,
  input  [2:0] AluOP,
  input  Clock,
  input  [31:0] Data_A,
  input  [31:0] Data_B,
  input  [31:0] Imm_Gen,
  input  [3:0] _30_14_12_Instructions,
  input  [4:0] _11_7_Instructions,
  input  [4:0] Rs1,
  input  [4:0] Rs2,
  input  clear,
  output [1:0] WB,
  output [2:0] M,
  output [3:0] EX,
  output [31:0] PC_2,
  output [31:0] Data_A_2,
  output [31:0] Data_B_2,
  output [31:0] Imm_Gen_2,
  output [3:0] _30_14_12_Instructions_2,
  output [4:0] _11_7_Instructions_2,
  output [4:0] Rs1_2,
  output [4:0] Rs2_2
);

  Register #(.width(9)) register_1 (
    .D({AluOP, Branch, MemWrite, MemRead, RegWrite, MemtoReg, ALUSrc}), .en(1'b1),
    .Q({EX[3:1], M, WB, EX[0]}), .clk(Clock), .clr(clear));
  Register #(.width(32)) register_2 (.D(Data_A), .en(1'b1), .Q(Data_A_2), .clk(Clock), .clr(clear));
  Register #(.width(32)) register_3 (.D(Data_B), .en(1'b1), .Q(Data_B_2), .clk(Clock), .clr(clear));
  Register #(.width(32)) register_4 (.D(Imm_Gen), .en(1'b1), .Q(Imm_Gen_2), .clk(Clock), .clr(clear));
  Register #(.width(4)) register_5 (
    .D(_30_14_12_Instructions), .en(1'b1), .Q(_30_14_12_Instructions_2), .clk(Clock), .clr(clear));
  Register #(.width(5)) register_6 (
    .D(_11_7_Instructions), .en(1'b1), .Q(_11_7_Instructions_2), .clk(Clock), .clr(clear));
  Register #(.width(5)) u_Rs1 (.D(Rs1), .en(1'b1), .Q(Rs1_2), .clk(Clock), .clr(clear));
  Register #(.width(5)) u_Rs2 (.D(Rs2), .en(1'b1), .Q(Rs2_2), .clk(Clock), .clr(clear));
  Register #(.width(32)) u_PC (.D(PC), .en(1'b1), .Q(PC_2), .clk(Clock), .clr(clear));
endmodule

module EX_MEM (
  input  [1:0] WB,
  input  [2:0] M,
  input  [31:0] AddSum,
  input  branchFromALU,
  input  [31:0] ALU_Result,
  input  [31:0] Data_B,
  input  [4:0] _11_7_Instructions,
  input  Clock,
  output [1:0] WB_2,
  output [2:0] M_2,
  output [31:0] AddSum_2,
  output branchFromALU_2,
  output [31:0] ALU_Result_2,
  output [31:0] Data_B_2,
  output [4:0] _11_7_Instructions_2
);

  Register #(.width(2)) u_WB (.D(WB), .en(1'b1), .Q(WB_2), .clk(Clock));  // open: clr
  Register #(.width(3)) u_M (.D(M), .en(1'b1), .Q(M_2), .clk(Clock));  // open: clr
  Register #(.width(32)) u_AddSum (.D(AddSum), .en(1'b1), .Q(AddSum_2), .clk(Clock));  // open: clr
  Register #(.width(1)) u_branchFromALU (.D(branchFromALU), .en(1'b1), .Q(branchFromALU_2), .clk(Clock));  // open: clr
  Register #(.width(32)) u_ALU_Result (.D(ALU_Result), .en(1'b1), .Q(ALU_Result_2), .clk(Clock));  // open: clr
  Register #(.width(32)) u_Data_B (.D(Data_B), .en(1'b1), .Q(Data_B_2), .clk(Clock));  // open: clr
  Register #(.width(5)) u__11_7_Instructions (
    .D(_11_7_Instructions), .en(1'b1), .Q(_11_7_Instructions_2), .clk(Clock));  // open: clr
endmodule

module MEM_WB (
  input  [1:0] WB,
  input  [31:0] Read_Data,
  input  [31:0] ALU_Result,
  input  [4:0] _11_7_Instructions,
  input  Clock,
  output [1:0] WB_2,
  output [31:0] Read_Data_2,
  output [31:0] ALU_Result_2,
  output [4:0] _11_7_Instructions_2
);

  Register #(.width(2)) u_WB (.D(WB), .en(1'b1), .Q(WB_2), .clk(Clock));  // open: clr
  Register #(.width(32)) u_Read_Data (.D(Read_Data), .en(1'b1), .Q(Read_Data_2), .clk(Clock));  // open: clr
  Register #(.width(32)) u_ALU_Result (.D(ALU_Result), .en(1'b1), .Q(ALU_Result_2), .clk(Clock));  // open: clr
  Register #(.width(5)) u__11_7_Instructions (
    .D(_11_7_Instructions), .en(1'b1), .Q(_11_7_Instructions_2), .clk(Clock));  // open: clr
endmodule

module hazard_Detection_Unit (
  input  Mem_Read,
  input  [4:0] Rs1,
  input  [4:0] Rs2,
  input  [4:0] Rd,
  output nStall
);

  wire and_1_out, comparator_1_eq, comparator_2_eq, not_1_out, or_1_out;

  Comparator #(.width(5)) comparator_1 (.a(Rs1), .b(Rd), .eq(comparator_1_eq));  // open: gt, lt
  Comparator #(.width(5)) comparator_2 (.a(Rs2), .b(Rd), .eq(comparator_2_eq));  // open: gt, lt
  or or_1 (or_1_out, comparator_1_eq, comparator_2_eq);
  and and_1 (and_1_out, Mem_Read, or_1_out);
  not not_1 (not_1_out, and_1_out);
  and and_2 (nStall, not_1_out, 1'b1);
endmodule

module forward_Unit (
  input  EX_MEM_RegWrite,
  input  [4:0] EX_MEM_Rd,
  input  [4:0] ID_EX_Rs1,
  input  [4:0] ID_EX_Rs2,
  input  MEM_WB_RegWrite,
  input  [4:0] MEM_WB_Rd,
  output [1:0] Forward_A,
  output [1:0] Forward_B
);

  wire comparator_1_eq, comparator_2_eq, comparator_3_eq, comparator_4_eq, comparator_5_eq, comparator_6_eq,
       not_1_out, not_2_out;
  wire [1:0] and_1_out, and_2_out;

  Comparator #(.width(5)) comparator_1 (.a({5{1'b0}}), .b(EX_MEM_Rd), .eq(comparator_1_eq));  // open: gt, lt
  Comparator #(.width(5)) comparator_2 (.a({5{1'b0}}), .b(MEM_WB_Rd), .eq(comparator_2_eq));  // open: gt, lt
  not not_1 (not_1_out, comparator_1_eq);
  Comparator #(.width(5)) comparator_3 (.a(EX_MEM_Rd), .b(ID_EX_Rs1), .eq(comparator_3_eq));  // open: gt, lt
  Comparator #(.width(5)) comparator_4 (.a(EX_MEM_Rd), .b(ID_EX_Rs2), .eq(comparator_4_eq));  // open: gt, lt
  not not_2 (not_2_out, comparator_2_eq);
  Comparator #(.width(5)) comparator_5 (.a(MEM_WB_Rd), .b(ID_EX_Rs1), .eq(comparator_5_eq));  // open: gt, lt
  Comparator #(.width(5)) comparator_6 (.a(MEM_WB_Rd), .b(ID_EX_Rs2), .eq(comparator_6_eq));  // open: gt, lt
  and and_1 (and_1_out[0], EX_MEM_RegWrite, not_1_out, comparator_3_eq);
  and and_2 (and_2_out[0], EX_MEM_RegWrite, not_1_out, comparator_4_eq);
  and and_3 (and_1_out[1], MEM_WB_RegWrite, not_2_out, comparator_5_eq);
  and and_4 (and_2_out[1], MEM_WB_RegWrite, not_2_out, comparator_6_eq);
  Multiplexer #(.select(2), .width(2), .disabled(0), .enable("false")) multiplexer_1 (
    .in0(2'b00), .in1(2'b10), .in2(2'b01), .in3(2'b00), .out(Forward_A), .sel(and_1_out));
  Multiplexer #(.select(2), .width(2), .disabled(0), .enable("false")) multiplexer_2 (
    .in0(2'b00), .in1(2'b10), .in2(2'b01), .in3(2'b00), .out(Forward_B), .sel(and_2_out));
endmodule
